# Fritzing sketch sheepBrainCircuit (saved by Fritzing 0.9.3b)
breadboards: 2

parts:
  Part1 = Adafruit MPR121
  Part2 = Adafruit Feather M0 RFM9x LoRa [part_number="Adafruit #3178 or #3179"]
  JP1 = Header 3 [package=screwterminal-3.5mm-3_lock.007s]
  JP2 = Header 5x2 [package=2x5-ra]
  JP3 = Header 8 [package=1x08_smd]
  SP1 = SPEAKER [package=pcb_mount_speaker]
  R3 = Resistor [tolerance=±5% resistance=3.3k package=THT]
  R4 = Resistor [tolerance=±5% resistance=3.3k package=THT]
  IC1 = Voltage Regulator [package=78xxl]
  D1 = Zener Diode [part_number=1N4732A breakdown_voltage=3.6V package="Melf DO-213 AB [SMD]"]
  R2 = Resistor [tolerance=±5% resistance=4.7k package="2512 [SMD]"]
  R1 = Resistor [tolerance=±5% resistance=1k package="2512 [SMD]"]
  Part3 = Adafruit MAX9744 20W Amplifier [part_number="Adafruit #1752"]
  SP2 = SPEAKER [package=pcb_mount_speaker]

nets:
  N1: Part1.ELEC7, JP3.1
  N2: Part1.ELEC6, JP3.2
  N3: Part1.ELEC5, JP3.3
  N4: Part1.ELEC4, JP3.4
  N5: Part1.ELEC3, JP3.5
  N6: Part1.ELEC2, JP3.6
  N7: Part1.ELEC1, JP3.7
  N8: Part1.ELEC0, JP3.8
  GND: Part1.GND, Part2.GND, JP1.2, IC1.GND, R1.Pin_0, Part3.GND
  3.3V: Part1.VIN, Part2.+3V3, R3.Pin_0, R4.Pin_0, Part3.VI2C
  SDA: Part1.SDA, Part2.SDA, JP2.3, R3.Pin_1, Part3.SDA
  SCL: Part1.SCL, Part2.SCL, JP2.5, R4.Pin_1, Part3.SCL
  N9: Part2.A0, R2.Pin_1, R1.Pin_1
  N10: Part2.VBUS, JP1.1, D1.cathode
  N11: SP1.+, Part3.LEFT+
  N12: SP1.-, Part3.LEFT-
  N13: IC1.IN, R2.Pin_0, Part3.VDD
  N14: IC1.OUT, D1.anode
  N15: Part3.RIGHT-, SP2.+
  N16: Part3.RIGHT+, SP2.-

notes:
  OctoWS2811 adapter
  23 22 19 18 17
  3.3v
  gnd
  SCL
  SDL
  5v supply
  5v
  12v battery/5.7
  touch ethernet jack
  5" long
  8" wires
  speaker
  pull up resistors
  Connections to Octo2811 Adapter and Teensy 3.5

custom parts:
  Adafruit MPR121: Add lots of touch sensors to your next microcontroller project with this easy-to-use 12-channel capacitive touch sensor breakout board, starring the MPR121. This chip can handle up to 12 individual touch pads. The MPR121 has support for only I2C, which can be implemented with nearly any microcontroller. You can select one of 4 addresses with the ADDR pin, for a total of 48 capacitive touch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
  Adafruit Feather M0 RFM9x LoRa: This is the Adafruit Feather M0 RFM95 LoRa Radio - our take on an microcontroller with a "Long Range (LoRa)" packet radio transceiver with built in USB and battery charging. Its an Adafruit Feather M0 with a 433Mhz or 900MHz radio module cooked in! Great for making wireless networks that are more flexible than Bluetooth LE and without the high power requirements of WiFi. We have other boards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
  Adafruit MAX9744 20W Amplifier: Pump up the volume with this 20W stereo amplifier! This slim little board has a class D amplifier onboard that can drive 2 channels of 4-8 ohm impedance speakers at 20W each. Power it with 5-12VDC using the onboard DC power jack and plug stereo line level into the 3.5mm stereo headphone jack and jam out with ease. Since it's class D, its completely cool-running, no heat sinks are required and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
