# Fritzing sketch sheepBrainCircuitNoBattery (saved by Fritzing 0.9.3b)
breadboards: 2

parts:
  Touch_controller = Adafruit MPR121
  M0_microcontroller_Musicmaker_and_GPS_adafruit_featherwing = Adafruit Feather M0 RFM9x LoRa [part_number="Adafruit #3178 or #3179"]
  JP1 = Header 3 [package=screwterminal-3.5mm-3_lock.007s]
  JP2 = Header 5x2 [package=2x5-ra]
  JP3 = Header 8 [package=1x08_smd]
  R3 = Resistor [tolerance=±5% resistance=3.3k package=THT]
  R4 = Resistor [tolerance=±5% resistance=3.3k package=THT]
  5v_voltage_regulator = Voltage Regulator [package=78xxl]
  D1 = Zener Diode [part_number=1N4732A breakdown_voltage=3.6V package="Melf DO-213 AB [SMD]"]
  Amplifier = Adafruit MAX9744 20W Amplifier [part_number="Adafruit #1752"]
  SP2 = SPEAKER [package=pcb_mount_speaker]
  SP1 = SPEAKER [package=pcb_mount_speaker]

nets:
  N1: Touch_controller.ELEC7, JP3.1
  N2: Touch_controller.ELEC6, JP3.2
  N3: Touch_controller.ELEC5, JP3.3
  N4: Touch_controller.ELEC4, JP3.4
  N5: Touch_controller.ELEC3, JP3.5
  N6: Touch_controller.ELEC2, JP3.6
  N7: Touch_controller.ELEC1, JP3.7
  N8: Touch_controller.ELEC0, JP3.8
  GND: Touch_controller.GND, M0_microcontroller_Musicmaker_and_GPS_adafruit_featherwing.GND, JP1.2, 5v_voltage_regulator.GND, Amplifier.GND
  3.3V: Touch_controller.VIN, M0_microcontroller_Musicmaker_and_GPS_adafruit_featherwing.+3V3, R3.Pin_0, R4.Pin_0, Amplifier.VI2C
  SDA: Touch_controller.SDA, M0_microcontroller_Musicmaker_and_GPS_adafruit_featherwing.SDA, JP2.3, R3.Pin_1, Amplifier.SDA
  SCL: Touch_controller.SCL, M0_microcontroller_Musicmaker_and_GPS_adafruit_featherwing.SCL, JP2.5, R4.Pin_1, Amplifier.SCL
  5v: M0_microcontroller_Musicmaker_and_GPS_adafruit_featherwing.VBUS, JP1.1, D1.cathode
  N9: 5v_voltage_regulator.IN, Amplifier.VDD
  N10: 5v_voltage_regulator.OUT, D1.anode
  N11: Amplifier.RIGHT-, SP2.+
  N12: Amplifier.RIGHT+, SP2.-
  N13: Amplifier.LEFT+, SP1.+
  N14: Amplifier.LEFT-, SP1.-

notes:
  OctoWS2811 adapter
  23 22 19 18 17
  3.3v
  gnd
  SCL
  SDL
  5v
  touch ethernet jack
  5" long
  8" wires
  speaker
  pull up resistors
  Connections to Octo2811 Adapter and Teensy 3.5
  Connections to touch sensors

custom parts:
  Adafruit MPR121: Add lots of touch sensors to your next microcontroller project with this easy-to-use 12-channel capacitive touch sensor breakout board, starring the MPR121. This chip can handle up to 12 individual touch pads. The MPR121 has support for only I2C, which can be implemented with nearly any microcontroller. You can select one of 4 addresses with the ADDR pin, for a total of 48 capacitive touch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
  Adafruit Feather M0 RFM9x LoRa: This is the Adafruit Feather M0 RFM95 LoRa Radio - our take on an microcontroller with a "Long Range (LoRa)" packet radio transceiver with built in USB and battery charging. Its an Adafruit Feather M0 with a 433Mhz or 900MHz radio module cooked in! Great for making wireless networks that are more flexible than Bluetooth LE and without the high power requirements of WiFi. We have other boards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
  Adafruit MAX9744 20W Amplifier: Pump up the volume with this 20W stereo amplifier! This slim little board has a class D amplifier onboard that can drive 2 channels of 4-8 ohm impedance speakers at 20W each. Power it with 5-12VDC using the onboard DC power jack and plug stereo line level into the 3.5mm stereo headphone jack and jam out with ease. Since it's class D, its completely cool-running, no heat sinks are required and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
