# Fritzing sketch sheepBrainCircuit (saved by Fritzing 0.9.3b)
breadboards: 2

parts:
  Part1 = Adafruit MPR121
  Part2 = Adafruit Feather M0 RFM9x LoRa [part_number="Adafruit #3178 or #3179"]
  Part3 = Adafruit MAX9744 20W Amplifier [part_number="Adafruit #1752"]
  D1 = Rectifier Diode [part_number=1N4001 package="300 mil [THT]"]
  R1 = Resistor [tolerance=±5% resistance=220 package="2512 [SMD]"]
  R2 = Resistor [tolerance=±5% resistance=220 package="2512 [SMD]"]

nets:
  GND: Part1.GND, Part2.GND, Part3.GND, R1.Pin_0
  VIN: Part1.VIN, Part2.+3V3, Part3.VI2C
  N1: Part1.SDA, Part2.SDA, Part3.SDA
  N2: Part1.SCL, Part2.SCL, Part3.SCL
  N3: Part2.A0, R1.Pin_1, R2.Pin_1
  N4: Part2.VBUS, D1.cathode
  N5: Part3.VDD, R2.Pin_0

custom parts:
  Adafruit MPR121: Add lots of touch sensors to your next microcontroller project with this easy-to-use 12-channel capacitive touch sensor breakout board, starring the MPR121. This chip can handle up to 12 individual touch pads. The MPR121 has support for only I2C, which can be implemented with nearly any microcontroller. You can select one of 4 addresses with the ADDR pin, for a total of 48 capacitive touch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
  Adafruit Feather M0 RFM9x LoRa: This is the Adafruit Feather M0 RFM95 LoRa Radio - our take on an microcontroller with a "Long Range (LoRa)" packet radio transceiver with built in USB and battery charging. Its an Adafruit Feather M0 with a 433Mhz or 900MHz radio module cooked in! Great for making wireless networks that are more flexible than Bluetooth LE and without the high power requirements of WiFi. We have other boards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
  Adafruit MAX9744 20W Amplifier: Pump up the volume with this 20W stereo amplifier! This slim little board has a class D amplifier onboard that can drive 2 channels of 4-8 ohm impedance speakers at 20W each. Power it with 5-12VDC using the onboard DC power jack and plug stereo line level into the 3.5mm stereo headphone jack and jam out with ease. Since it's class D, its completely cool-running, no heat sinks are required and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
